# Fritzing sketch ultrlight (saved by Fritzing 0.9.0b)
breadboards: 1

parts:
  Componente2 = Arduino Uno (Rev3)
  LED1 = LED - 5mm [color="Red (660nm)" package="5 mm [THT]"]
  LED2 = LED - 5mm [color="Yellow (595nm)" package="5 mm [THT]"]
  J1 = Piezo Speaker
  part = LED - 5mm [color="Green (570nm)" package="5 mm [THT]"]
  Componente3 = SRF05 Ultrasonic Rangefinder

nets:
  N1: Componente2.D11_PWM/MOSI, Componente3.Echo
  N2: Componente2.D12/MISO, Componente3.Trig
  GND: Componente2.GND, LED1.anode, LED2.anode, J1.pin1, part.anode, Componente3.GND
  N3: Componente2.D1/TX, part.cathode
  N4: Componente2.D2, LED2.cathode
  N5: Componente2.D3_PWM, LED1.cathode
  N6: Componente2.D5_PWM, J1.pin2
  5V: Componente2.5V, Componente3.VCC
